// Logisim project Lab10_247-207-VA_LeonardoFusser.circ as structural Verilog: 1 circuit, main circuit main
module main (
);

  wire CLK_out, FF0_q, FF1_q, FF2_q, FF3_q, nor_1_out;

  nor nor_1 (nor_1_out, FF2_q, FF1_q, FF0_q);
  Clock CLK (.out(CLK_out));
  D_Flip_Flop FF0 (.clk(CLK_out), .D(nor_1_out), .Q(FF0_q));  // open: Qn, preset, en, reset
  LED led_1 (.in(FF0_q));
  D_Flip_Flop FF1 (.clk(CLK_out), .D(FF0_q), .Q(FF1_q));  // open: Qn, preset, en, reset
  LED led_2 (.in(FF1_q));
  LED led_3 (.in(FF2_q));
  D_Flip_Flop FF2 (.clk(CLK_out), .D(FF1_q), .Q(FF2_q));  // open: Qn, preset, en, reset
  LED led_4 (.in(FF3_q));
  D_Flip_Flop FF3 (.clk(CLK_out), .D(FF2_q), .Q(FF3_q));  // open: Qn, preset, en, reset

  // Notes on the sheet:
  //   Simulation made by: Leonardo Fusser
  //   For: Subash Handa
  //   Computational Logic
  //   Lab4Online, simulation #1
  //   (Q0+Q1+Q2)'
endmodule
