// Logisim project Lab11_247-207-VA_LeonardoFusser.circ as structural Verilog: 1 circuit, main circuit main
module main (
);

  wire BC_out, CLK_out, Decoder_out, FF0__A_q, FF1__B_q, FF2__C_q, not_1_out;

  Clock CLK (.out(CLK_out));
  and BC (BC_out, FF2__C_q, FF1__B_q);
  J_K_Flip_Flop FF0__A (.J(BC_out), .clk(CLK_out), .K(BC_out), .Q(FF0__A_q));  // open: Qn, preset, en, reset
  J_K_Flip_Flop FF1__B (.J(FF2__C_q), .clk(CLK_out), .K(FF2__C_q), .Q(FF1__B_q));  // open: Qn, preset, en, reset
  J_K_Flip_Flop FF2__C (.J(1'b1), .clk(CLK_out), .K(1'b1), .Q(FF2__C_q));  // open: Qn, preset, en, reset
  LED When_ABC___6 (.in(Decoder_out));
  and Decoder (Decoder_out, FF0__A_q, FF1__B_q, not_1_out);
  not not_1 (not_1_out, FF2__C_q);

  // Notes on the sheet:
  //   For: Subash Handa
  //   Computational Logic
  //   Online Lab #5, Simulation 1
  //   PWR
  //   Simulation made by: Leonardo Fusser (1946995)
endmodule
