// Logisim project Lab12-Simulation2_247-207-VA_LeonardoFusser.circ as structural Verilog: 1 circuit, main circuit main
module main (
  input  INPUT,
  input  RIGHT_LEFT
);

  wire and_1_out, and_2_out, and_3_out, and_4_out, and_5_out, and_6_out, and_7_out, and_8_out, CLK_out,
       FF1_q, FF2_q, FF3_q, FF4_q, not_1_out, or_1_out, or_2_out, or_3_out, or_4_out;

  not not_1 (not_1_out, RIGHT_LEFT);
  and and_1 (and_1_out, not_1_out, FF2_q);
  and and_2 (and_2_out, INPUT, RIGHT_LEFT);
  or or_1 (or_1_out, and_2_out, and_1_out);
  Clock CLK (.out(CLK_out));
  and and_3 (and_3_out, FF1_q, RIGHT_LEFT);
  and and_4 (and_4_out, not_1_out, FF3_q);
  or or_2 (or_2_out, and_3_out, and_4_out);
  D_Flip_Flop FF1 (.clk(CLK_out), .D(or_1_out), .Q(FF1_q));  // open: Qn, preset, en, reset
  LED Q0 (.in(FF1_q));
  and and_5 (and_5_out, FF2_q, RIGHT_LEFT);
  or or_3 (or_3_out, and_5_out, and_6_out);
  D_Flip_Flop FF2 (.clk(CLK_out), .D(or_2_out), .Q(FF2_q));  // open: Qn, preset, en, reset
  LED Q1 (.in(FF2_q));
  and and_6 (and_6_out, not_1_out, FF4_q);
  and and_7 (and_7_out, FF3_q, RIGHT_LEFT);
  D_Flip_Flop FF3 (.clk(CLK_out), .D(or_3_out), .Q(FF3_q));  // open: Qn, preset, en, reset
  LED Q2 (.in(FF3_q));
  and and_8 (and_8_out, not_1_out, INPUT);
  or or_4 (or_4_out, and_7_out, and_8_out);
  D_Flip_Flop FF4 (.clk(CLK_out), .D(or_4_out), .Q(FF4_q));  // open: Qn, preset, en, reset
  LED Q3 (.in(FF4_q));

  // Notes on the sheet:
  //   For: Subash Handa
  //   Computational Logic
  //   Simulation made by: Leonardo Fusser (1946995)
  //   OnlineLab6, simulation #2
  //   (1: Right/0: Left)
endmodule
