// Logisim project Lab7-Simulation1_247-207-VA_LeonardoFusser.circ as structural Verilog: 1 circuit, main circuit main
module main (
);

  wire CLCK_out, FF0_q, FF1_q, FF2_q, FF3_q;

  Clock CLCK (.out(CLCK_out));
  J_K_Flip_Flop #(.trigger("falling")) FF1 (.J(1'b1), .clk(FF0_q), .K(1'b1), .Q(FF1_q));  // open: Qn, preset, en, reset
  J_K_Flip_Flop #(.trigger("falling")) FF0 (
    .J(1'b1), .clk(CLCK_out), .K(1'b1), .Q(FF0_q));  // open: Qn, preset, en, reset
  J_K_Flip_Flop #(.trigger("falling")) FF2 (.J(1'b1), .clk(FF1_q), .K(1'b1), .Q(FF2_q));  // open: Qn, preset, en, reset
  J_K_Flip_Flop #(.trigger("falling")) FF3 (.J(1'b1), .clk(FF2_q), .K(1'b1), .Q(FF3_q));  // open: Qn, preset, en, reset
  LED MSB (.in(FF3_q));
  LED led_1 (.in(FF2_q));
  LED led_2 (.in(FF1_q));
  LED LSB (.in(FF0_q));

  // Notes on the sheet:
  //   For: Subash Handa
  //   Computational Logic
  //   +5V
  //   Simulation made by: Leonardo Fusser (1946995)
  //   Online lab #1, Simulation 1
endmodule
