// Logisim project Lab7-Simulation2_247-207-VA_LeonardoFusser.circ as structural Verilog: 1 circuit, main circuit main
module main (
);

  wire CLCK_out, FF0_q, FF1_q, FF2_q, FF3_q, nand_1_out, not_1_out, not_2_out;

  LED MSB (.in(FF3_q));
  Clock CLCK (.out(CLCK_out));
  not not_1 (not_1_out, 1'b1);
  LED led_1 (.in(FF2_q));
  J_K_Flip_Flop #(.trigger("falling")) FF0 (
    .J(1'b1), .clk(CLCK_out), .K(1'b1), .Q(FF0_q), .reset(not_1_out));  // open: Qn, preset, en
  LED led_2 (.in(FF1_q));
  J_K_Flip_Flop #(.trigger("falling")) FF1 (
    .J(1'b1), .clk(FF0_q), .K(1'b1), .Q(FF1_q), .reset(not_1_out));  // open: Qn, preset, en
  J_K_Flip_Flop #(.trigger("falling")) FF2 (
    .J(1'b1), .clk(FF1_q), .K(1'b1), .Q(FF2_q), .reset(not_2_out));  // open: Qn, preset, en
  LED LSB (.in(FF0_q));
  J_K_Flip_Flop #(.trigger("falling")) FF3 (
    .J(1'b1), .clk(FF2_q), .K(1'b1), .Q(FF3_q), .reset(not_2_out));  // open: Qn, preset, en
  nand nand_1 (nand_1_out, FF2_q, FF3_q);
  not not_2 (not_2_out, nand_1_out);

  // Notes on the sheet:
  //   For: Subash Handa
  //   Computational Logic
  //   Online lab #1, Simulation 2
  //   +5V
  //   Simulation made by: Leonardo Fusser (1946995)
  //   12 decoder
endmodule
