// Logisim project Lab8_247-207-VA_LeonardoFusser.circ as structural Verilog: 1 circuit, main circuit main
module main (
);

  wire and_1_out, and_2_out, CLK_out, FF0_A_q, FF0_A_qn, FF1_B_q, FF2_C_q, or_1_out;

  LED A (.in(FF0_A_q));
  LED C (.in(FF2_C_q));
  LED B (.in(FF1_B_q));
  Clock CLK (.out(CLK_out));
  and and_1 (and_1_out, FF2_C_q, FF1_B_q);
  J_K_Flip_Flop FF0_A (.J(and_1_out), .clk(CLK_out), .K(1'b1), .Q(FF0_A_q), .Qn(FF0_A_qn));  // open: preset, en, reset
  and and_2 (and_2_out, FF2_C_q, FF0_A_qn);
  or or_1 (or_1_out, FF2_C_q, FF0_A_q);
  J_K_Flip_Flop FF1_B (.J(and_2_out), .clk(CLK_out), .K(or_1_out), .Q(FF1_B_q));  // open: Qn, preset, en, reset
  J_K_Flip_Flop FF2_C (.J(FF0_A_qn), .clk(CLK_out), .K(1'b1), .Q(FF2_C_q));  // open: Qn, preset, en, reset

  // Notes on the sheet:
  //   Simulation made by: Leonardo Fusser (1946995)
  //   For: Subash Handa
  //   Computational Logic
  //   Online Lab #2, Simulation 1
  //   (B)(C)
  //   (A')(C)
  //   (A+C)
endmodule
