// Logisim project Lab9_247-207-VA_LeonardoFusser.circ as structural Verilog: 1 circuit, main circuit main
module main (
  input  S
);

  wire BC_out, CLK_out, FF0_A_q, FF1_B_q, FF2_C_q, not_1_out, S_prime_B_BC_out, S_prime_B_out, S_prime_C_out;

  Clock CLK (.out(CLK_out));
  not not_1 (not_1_out, S);
  and S_prime_B (S_prime_B_out, not_1_out, FF1_B_q);
  and BC (BC_out, FF1_B_q, FF2_C_q);
  J_K_Flip_Flop FF0_A (
    .J(S_prime_B_BC_out), .clk(CLK_out), .K(S_prime_B_BC_out), .Q(FF0_A_q));  // open: Qn, preset, en, reset
  or S_prime_B_BC (S_prime_B_BC_out, S_prime_B_out, BC_out);
  or S_prime_C (S_prime_C_out, not_1_out, FF2_C_q);
  J_K_Flip_Flop FF1_B (
    .J(S_prime_C_out), .clk(CLK_out), .K(S_prime_C_out), .Q(FF1_B_q));  // open: Qn, preset, en, reset
  LED B (.in(FF1_B_q));
  LED C (.in(FF2_C_q));
  LED A (.in(FF0_A_q));
  J_K_Flip_Flop FF2_C (.J(S), .clk(CLK_out), .K(not_1_out), .Q(FF2_C_q));  // open: Qn, preset, en, reset

  // Notes on the sheet:
  //   For: Subash Handa
  //   Compuataional Logic
  //   Online Lab #3, Simulation 1
  //   Simulation made by: Leonardo Fusser (1946995)
endmodule
